// Logisim project Project_6_circuit ray.circ as structural Verilog: 25 circuits, main circuit main
module main (
  output HALTED,
  output [63:0] rax,
  output [63:0] rcx,
  output [63:0] rdx,
  output [63:0] rbx,
  output [63:0] rsp,
  output [63:0] rbp,
  output [63:0] rsi,
  output [63:0] rdi,
  output [63:0] r8,
  output [63:0] r9,
  output [63:0] r10,
  output [63:0] r11,
  output [63:0] r12,
  output [63:0] r13,
  output [63:0] r14
);

  wire and_1_out, clock_1_out, comparator_1_eq, comparator_2_lt, comparator_3_eq, comparator_4_lt,
       comparator_5_gt, comparator_6_eq, comparator_7_eq, comparator_8_gt, comparator_9_eq,
       controlled_buffer_1_out, controlled_buffer_2_out, controlled_buffer_3_out, controlled_buffer_4_out,
       controlled_buffer_5_out, controlled_buffer_6_out, controlled_buffer_7_out, controlled_buffer_8_out,
       controlled_buffer_9_out, controlled_buffer_10_out, controlled_buffer_11_out, execute_1_conditional,
       not_1_out, not_2_out, not_3_out, pcupdate_1_regupdate;
  wire [3:0] fetchmain_1_icode, fetchmain_1_ifun, fetchmain_1_ra, fetchmain_1_rb, writeback_1_dste,
       writeback_1_dstm;
  wire [7:0] counter_1_q;
  wire [11:0] fetchmain_1_valp, pcupdate_1_newpc, register_1_q;
  wire [63:0] decode_1_vala, decode_1_valb, execute_1_vale, fetchmain_1_valc, memory_1_valm;

  Clock clock_1 (.out(clock_1_out));
  not not_1 (not_1_out, HALTED);
  assign controlled_buffer_1_out = not_1_out ? clock_1_out : 1'bz;  // Controlled_Buffer controlled_buffer_1
  Register #(.width(12)) register_1 (
    .D(pcupdate_1_newpc), .clk(pcupdate_1_regupdate), .Q(register_1_q));  // open: en, clr
  Counter counter_1 (.clr(comparator_9_eq), .clk(not_2_out), .Q(counter_1_q));  // open: load, up, count, D, carry
  not not_2 (not_2_out, controlled_buffer_1_out);
  assign controlled_buffer_2_out = comparator_2_lt ? controlled_buffer_1_out : 1'bz;  // Controlled_Buffer controlled_buffer_2
  fetchMain fetchmain_1 (
    .PC(register_1_q), .clk(controlled_buffer_2_out), .iCode(fetchmain_1_icode), .haltstate(HALTED),
    .iFun(fetchmain_1_ifun), .rA(fetchmain_1_ra), .rB(fetchmain_1_rb), .ValC(fetchmain_1_valc),
    .valP(fetchmain_1_valp));  // open: increment
  Comparator #(.width(4)) comparator_1 (.a(fetchmain_1_icode), .b(4'b0001), .eq(comparator_1_eq));  // open: gt, lt
  not not_3 (not_3_out, comparator_1_eq);
  Comparator comparator_2 (.a(counter_1_q), .b(8'ha), .lt(comparator_2_lt));  // open: gt, eq
  Comparator comparator_3 (.a(counter_1_q), .b(8'ha), .eq(comparator_3_eq));  // open: gt, lt
  Comparator comparator_4 (.a(counter_1_q), .b(8'h13), .lt(comparator_4_lt));  // open: gt, eq
  Comparator comparator_5 (.a(counter_1_q), .b(8'ha), .gt(comparator_5_gt));  // open: eq, lt
  Comparator comparator_6 (.a(counter_1_q), .b(8'h13), .eq(comparator_6_eq));  // open: gt, lt
  Comparator comparator_7 (.a(counter_1_q), .b(8'h14), .eq(comparator_7_eq));  // open: gt, lt
  Comparator comparator_8 (.a(counter_1_q), .b(8'h14), .gt(comparator_8_gt));  // open: eq, lt
  Comparator comparator_9 (.a(counter_1_q), .b(8'h17), .eq(comparator_9_eq));  // open: gt, lt
  assign controlled_buffer_3_out = controlled_buffer_4_out ? controlled_buffer_1_out : 1'bz;  // Controlled_Buffer controlled_buffer_3
  assign controlled_buffer_4_out = not_3_out ? comparator_3_eq : 1'bz;  // Controlled_Buffer controlled_buffer_4
  assign controlled_buffer_5_out = not_3_out ? comparator_6_eq : 1'bz;  // Controlled_Buffer controlled_buffer_5
  assign controlled_buffer_6_out = not_3_out ? comparator_7_eq : 1'bz;  // Controlled_Buffer controlled_buffer_6
  assign controlled_buffer_7_out = controlled_buffer_6_out ? controlled_buffer_1_out : 1'bz;  // Controlled_Buffer controlled_buffer_7
  and and_1 (and_1_out, comparator_4_lt, comparator_5_gt);
  assign controlled_buffer_8_out = not_3_out ? and_1_out : 1'bz;  // Controlled_Buffer controlled_buffer_8
  Decode decode_1 (
    .rA(fetchmain_1_ra), .valM(memory_1_valm), .valE(execute_1_vale), .rB(fetchmain_1_rb),
    .dstM(writeback_1_dstm), .dstE(writeback_1_dste), .iCode(fetchmain_1_icode),
    .clk(controlled_buffer_7_out), .valA(decode_1_vala), .valB(decode_1_valb), .rax(rax), .rcx(rcx),
    .rdx(rdx), .rbx(rbx), .rsp(rsp), .rbp(rbp), .rsi(rsi), .rdi(rdi), .r8(r8), .r9(r9), .r10(r10), .r11(r11),
    .r12(r12), .r13(r13), .r14(r14));
  Execute execute_1 (
    .clk(controlled_buffer_3_out), .ifun(fetchmain_1_ifun), .icode(fetchmain_1_icode), .valA(decode_1_vala),
    .valB(decode_1_valb), .valC(fetchmain_1_valc), .valE(execute_1_vale), .conditional(execute_1_conditional));  // open: zero, sign, overflow
  assign controlled_buffer_9_out = controlled_buffer_8_out ? controlled_buffer_1_out : 1'bz;  // Controlled_Buffer controlled_buffer_9
  Memory memory_1 (
    .icode(fetchmain_1_icode), .valE(execute_1_vale), .valA(decode_1_vala), .valP(fetchmain_1_valp),
    .clk(controlled_buffer_9_out), .valM(memory_1_valm));
  assign controlled_buffer_10_out = controlled_buffer_5_out ? controlled_buffer_1_out : 1'bz;  // Controlled_Buffer controlled_buffer_10
  assign controlled_buffer_11_out = comparator_8_gt ? controlled_buffer_1_out : 1'bz;  // Controlled_Buffer controlled_buffer_11
  writeBack writeback_1 (
    .rA(fetchmain_1_ra), .rB(fetchmain_1_rb), .icode(fetchmain_1_icode), .clk(controlled_buffer_10_out),
    .dstE(writeback_1_dste), .dstM(writeback_1_dstm));
  PCupdate pcupdate_1 (
    .valP(fetchmain_1_valp), .valC(fetchmain_1_valc), .cond(execute_1_conditional),
    .icode(fetchmain_1_icode), .valM(memory_1_valm), .clk(controlled_buffer_11_out),
    .newPC(pcupdate_1_newpc), .regupdate(pcupdate_1_regupdate));
endmodule

module InstructionDecoder (
  input  [7:0] in_1,
  output Halt,
  output nop,
  output rrmovq,
  output irmovq,
  output rmmovq,
  output mrmovq,
  output addq,
  output subq,
  output andq,
  output xorq,
  output jmp,
  output jle,
  output jl,
  output je,
  output jne,
  output jge,
  output jg,
  output pushq,
  output popq,
  output ret
);

  wire not_1_out, not_2_out, not_3_out, not_4_out, not_5_out, not_6_out, not_7_out, not_8_out;

  not not_1 (not_1_out, in_1[0]);
  not not_2 (not_2_out, in_1[1]);
  not not_3 (not_3_out, in_1[2]);
  not not_4 (not_4_out, in_1[3]);
  not not_5 (not_5_out, in_1[4]);
  not not_6 (not_6_out, in_1[5]);
  not not_7 (not_7_out, in_1[6]);
  not not_8 (not_8_out, in_1[7]);
  and and_1 (Halt, not_1_out, not_2_out, not_3_out, not_4_out, not_5_out, not_6_out, not_7_out, not_8_out);
  and and_2 (nop, not_1_out, not_2_out, not_3_out, not_4_out, in_1[4], not_6_out, not_7_out, not_8_out);
  and and_3 (rrmovq, not_1_out, not_2_out, not_3_out, not_4_out, not_5_out, in_1[5], not_7_out, not_8_out);
  and and_4 (irmovq, not_1_out, not_2_out, not_3_out, not_4_out, in_1[4], in_1[5], not_7_out, not_8_out);
  and and_5 (rmmovq, not_1_out, not_2_out, not_3_out, not_4_out, not_5_out, not_6_out, in_1[6], not_8_out);
  and and_6 (mrmovq, not_1_out, not_2_out, not_3_out, not_4_out, in_1[4], not_6_out, in_1[6], not_8_out);
  and and_7 (addq, not_1_out, not_2_out, not_3_out, not_4_out, not_5_out, in_1[5], in_1[6], not_8_out);
  and and_8 (subq, in_1[0], not_2_out, not_3_out, not_4_out, not_5_out, in_1[5], in_1[6], not_8_out);
  and and_9 (andq, not_1_out, in_1[1], not_3_out, not_4_out, not_5_out, in_1[5], in_1[6], not_8_out);
  and and_10 (xorq, in_1[0], in_1[1], not_3_out, not_4_out, not_5_out, in_1[5], in_1[6], not_8_out);
  and and_11 (jmp, not_1_out, not_2_out, not_3_out, not_4_out, in_1[4], in_1[5], in_1[6], not_8_out);
  and and_12 (jle, in_1[0], not_2_out, not_3_out, not_4_out, in_1[4], in_1[5], in_1[6], not_8_out);
  and and_13 (jl, not_1_out, in_1[1], not_3_out, not_4_out, in_1[4], in_1[5], in_1[6], not_8_out);
  and and_14 (je, in_1[0], in_1[1], not_3_out, not_4_out, in_1[4], in_1[5], in_1[6], not_8_out);
  and and_15 (jne, not_1_out, not_2_out, in_1[2], not_4_out, in_1[4], in_1[5], in_1[6], not_8_out);
  and and_16 (jge, in_1[0], not_2_out, in_1[2], not_4_out, in_1[4], in_1[5], in_1[6], not_8_out);
  and and_17 (jg, not_1_out, in_1[1], in_1[2], not_4_out, in_1[4], in_1[5], in_1[6], not_8_out);
  and and_18 (pushq, not_1_out, not_2_out, not_3_out, not_4_out, not_5_out, in_1[5], not_7_out, in_1[7]);
  and and_19 (popq, not_1_out, not_2_out, not_3_out, not_4_out, in_1[4], in_1[5], not_7_out, in_1[7]);
  and and_20 (ret, not_1_out, in_1[1], in_1[2], not_4_out, in_1[4], in_1[5], in_1[6], in_1[7]);
endmodule

module ValPDecoder (
  input  [3:0] icode,
  output STOP,
  output [11:0] P_inc
);

  wire call_out, cmov_out, irmovq_out, jXX_out, mrmovq_out, nine_inc_out, nop_out, not_1_out, not_2_out,
       not_3_out, not_4_out, one_inc_out, OPq_out, popq_out, pushq_out, ret_out, rmmovq_out, ten_inc_out,
       two_inc_out;

  not not_1 (not_1_out, icode[0]);
  not not_2 (not_2_out, icode[1]);
  not not_3 (not_3_out, icode[2]);
  not not_4 (not_4_out, icode[3]);
  and halt (STOP, not_1_out, not_2_out, not_3_out, not_4_out);
  and nop (nop_out, icode[0], not_2_out, not_3_out, not_4_out);
  and cmov (cmov_out, not_1_out, icode[1], not_3_out, not_4_out);
  and irmovq (irmovq_out, icode[0], icode[1], not_3_out, not_4_out);
  and rmmovq (rmmovq_out, not_1_out, not_2_out, icode[2], not_4_out);
  and mrmovq (mrmovq_out, icode[0], not_2_out, icode[2], not_4_out);
  and OPq (OPq_out, not_1_out, icode[1], icode[2], not_4_out);
  and jXX (jXX_out, icode[0], icode[1], icode[2], not_4_out);
  and call (call_out, not_1_out, not_2_out, not_3_out, icode[3]);
  and ret (ret_out, icode[0], not_2_out, not_3_out, icode[3]);
  and pushq (pushq_out, not_1_out, icode[1], not_3_out, icode[3]);
  and popq (popq_out, icode[0], icode[1], not_3_out, icode[3]);
  or one_inc (one_inc_out, nop_out, ret_out);
  or two_inc (two_inc_out, cmov_out, OPq_out, pushq_out, popq_out);
  or nine_inc (nine_inc_out, call_out, jXX_out);
  or ten_inc (ten_inc_out, irmovq_out, rmmovq_out, mrmovq_out);
  or bit0 (P_inc[0], one_inc_out, nine_inc_out);
  or bit1 (P_inc[1], two_inc_out, ten_inc_out);
  or bit4 (P_inc[3], nine_inc_out, ten_inc_out);

  assign {P_inc[11:4], P_inc[2]} = {9{1'b0}};

  // Notes on the sheet:
  //   spits out increment in binary
  //   This decodes iCode so that we know PC increment value
endmodule

module fetchEnable (
  input  [7:0] bytetrack,
  input  [7:0] p_inc,
  input  clk,
  input  [3:0] icode,
  input  [3:0] iFUN,
  output byte0,
  output byte1,
  output byte2,
  output byte3,
  output byte4,
  output byte5,
  output byte6,
  output byte7,
  output byte8,
  output byte9,
  output resetEqual
);

  wire byte1en_out, bytevalC_out, instructiondecodesimple_1_call, instructiondecodesimple_1_cmovxx,
       instructiondecodesimple_1_irmovq, instructiondecodesimple_1_jxx, instructiondecodesimple_1_mrmovq,
       instructiondecodesimple_1_opq, instructiondecodesimple_1_popq, instructiondecodesimple_1_pushq,
       instructiondecodesimple_1_rmmovq, instructiondecodesimple_1_rrmovq, not_1_out, not_2_out, not_3_out,
       not_4_out, undriven;
  wire [7:0] counter_1_q;

  instructionDecodeSimple instructiondecodesimple_1 (
    .icode(icode), .ifun(iFUN), .rrmovq(instructiondecodesimple_1_rrmovq),
    .irmovq(instructiondecodesimple_1_irmovq), .rmmovq(instructiondecodesimple_1_rmmovq),
    .mrmovq(instructiondecodesimple_1_mrmovq), .OPq(instructiondecodesimple_1_opq),
    .jxx(instructiondecodesimple_1_jxx), .cmovXX(instructiondecodesimple_1_cmovxx),
    .call(instructiondecodesimple_1_call), .pushq(instructiondecodesimple_1_pushq),
    .popq(instructiondecodesimple_1_popq));  // open: halt, nop, ret
  Counter counter_1 (
    .clr(resetEqual), .up(undriven), .count(clk), .clk(clk), .D(bytetrack), .Q(counter_1_q));  // open: load, carry
  or byte1en (byte1en_out, instructiondecodesimple_1_mrmovq, instructiondecodesimple_1_rrmovq, instructiondecodesimple_1_irmovq, instructiondecodesimple_1_rmmovq, instructiondecodesimple_1_opq, instructiondecodesimple_1_pushq, instructiondecodesimple_1_popq, instructiondecodesimple_1_cmovxx);
  or bytevalC (bytevalC_out, instructiondecodesimple_1_irmovq, instructiondecodesimple_1_rmmovq, instructiondecodesimple_1_mrmovq, instructiondecodesimple_1_jxx, instructiondecodesimple_1_call);
  not not_1 (not_1_out, counter_1_q[0]);
  not not_2 (not_2_out, counter_1_q[1]);
  not not_3 (not_3_out, counter_1_q[2]);
  not not_4 (not_4_out, counter_1_q[3]);
  Comparator comparator_1 (.a(counter_1_q), .b(p_inc), .eq(resetEqual));  // open: gt, lt
  and and_1 (byte0, not_1_out, not_2_out, not_3_out, not_4_out);
  and and_2 (byte1, counter_1_q[0], not_2_out, not_3_out, not_4_out, byte1en_out);
  and and_3 (byte2, not_1_out, counter_1_q[1], not_3_out, not_4_out, bytevalC_out);
  and and_4 (byte3, counter_1_q[0], counter_1_q[1], not_3_out, not_4_out, bytevalC_out);
  and and_5 (byte4, not_1_out, not_2_out, counter_1_q[2], not_4_out, bytevalC_out);
  and and_6 (byte5, counter_1_q[0], not_2_out, counter_1_q[2], not_4_out, bytevalC_out);
  and and_7 (byte6, not_1_out, counter_1_q[1], counter_1_q[2], not_4_out, bytevalC_out);
  and and_8 (byte7, counter_1_q[0], counter_1_q[1], counter_1_q[2], not_4_out, bytevalC_out);
  and and_9 (byte8, not_1_out, not_2_out, not_3_out, counter_1_q[3], bytevalC_out);
  and and_10 (byte9, counter_1_q[0], not_2_out, not_3_out, counter_1_q[3], bytevalC_out);
  // AND_Gate byte10 has open pins: in0=not_1_out, in1=counter_1_q[1], in2=not_3_out, in3=counter_1_q[3], out=open
  // AND_Gate byte11 has open pins: in0=counter_1_q[0], in1=counter_1_q[1], in2=not_3_out, in3=counter_1_q[3], out=open

  // Notes on the sheet:
  //   equal?
  //   add clock as input so enable only works when clock is ticked.
  //   use input value from icode to determine if  registers 1 - 10 are enabled
endmodule

module instructionDecodeSimple (
  input  [3:0] icode,
  input  [3:0] ifun,
  output halt,
  output nop,
  output rrmovq,
  output irmovq,
  output rmmovq,
  output mrmovq,
  output OPq,
  output jxx,
  output cmovXX,
  output call,
  output ret,
  output pushq,
  output popq
);

  wire and_1_out, cmov2_out, not_1_out, not_2_out, not_3_out, not_4_out, not_5_out, not_6_out, not_7_out,
       not_8_out, or_1_out;

  not not_1 (not_1_out, icode[0]);
  not not_2 (not_2_out, icode[1]);
  not not_3 (not_3_out, icode[2]);
  not not_4 (not_4_out, icode[3]);
  and halt0 (halt, not_1_out, not_2_out, not_3_out, not_4_out);
  and nop1 (nop, icode[0], not_2_out, not_3_out, not_4_out);
  and cmov2 (cmov2_out, not_1_out, icode[1], not_3_out, not_4_out);
  and irmovq3 (irmovq, icode[0], icode[1], not_3_out, not_4_out);
  and rmmovq4 (rmmovq, not_1_out, not_2_out, icode[2], not_4_out);
  and mrmovq5 (mrmovq, icode[0], not_2_out, icode[2], not_4_out);
  and OPq6 (OPq, not_1_out, icode[1], icode[2], not_4_out);
  and jXX7 (jxx, icode[0], icode[1], icode[2], not_4_out);
  and call8 (call, not_1_out, not_2_out, not_3_out, icode[3]);
  and ret9 (ret, icode[0], not_2_out, not_3_out, icode[3]);
  and pushq10 (pushq, not_1_out, icode[1], not_3_out, icode[3]);
  and popq11 (popq, icode[0], icode[1], not_3_out, icode[3]);
  not not_5 (not_5_out, ifun[0]);
  not not_6 (not_6_out, ifun[1]);
  not not_7 (not_7_out, ifun[2]);
  not not_8 (not_8_out, ifun[3]);
  or or_1 (or_1_out, ifun[0], ifun[1], ifun[2], ifun[3]);
  and and_1 (and_1_out, not_5_out, not_6_out, not_7_out, not_8_out);
  and and_2 (rrmovq, cmov2_out, and_1_out);
  and and_3 (cmovXX, cmov2_out, or_1_out);
endmodule

module oppositeNULL (
  input  clk,
  input  [3:0] iFUN,
  output byte0,
  output byte1,
  output byte2,
  output byte3,
  output byte4,
  output byte5,
  output byte6,
  output byte7,
  output byte8,
  output byte9,
  output resetEqual
);

  wire byte1en_out, bytevalC_out, instructiondecodesimple_1_call, instructiondecodesimple_1_cmovxx,
       instructiondecodesimple_1_irmovq, instructiondecodesimple_1_jxx, instructiondecodesimple_1_mrmovq,
       instructiondecodesimple_1_opq, instructiondecodesimple_1_popq, instructiondecodesimple_1_pushq,
       instructiondecodesimple_1_rmmovq, instructiondecodesimple_1_rrmovq, not_1_out, not_2_out, not_3_out,
       not_4_out, undriven;
  wire [7:0] counter_1_q;

  instructionDecodeSimple instructiondecodesimple_1 (
    .icode(4'b0011), .ifun(iFUN), .rrmovq(instructiondecodesimple_1_rrmovq),
    .irmovq(instructiondecodesimple_1_irmovq), .rmmovq(instructiondecodesimple_1_rmmovq),
    .mrmovq(instructiondecodesimple_1_mrmovq), .OPq(instructiondecodesimple_1_opq),
    .jxx(instructiondecodesimple_1_jxx), .cmovXX(instructiondecodesimple_1_cmovxx),
    .call(instructiondecodesimple_1_call), .pushq(instructiondecodesimple_1_pushq),
    .popq(instructiondecodesimple_1_popq));  // open: halt, nop, ret
  Counter counter_1 (
    .clr(resetEqual), .up(undriven), .count(clk), .clk(clk), .D({8{1'b0}}), .Q(counter_1_q));  // open: load, carry
  or byte1en (byte1en_out, instructiondecodesimple_1_rrmovq, instructiondecodesimple_1_irmovq, instructiondecodesimple_1_rmmovq, instructiondecodesimple_1_opq, instructiondecodesimple_1_pushq, instructiondecodesimple_1_popq, instructiondecodesimple_1_cmovxx);
  or bytevalC (bytevalC_out, instructiondecodesimple_1_irmovq, instructiondecodesimple_1_rmmovq, instructiondecodesimple_1_mrmovq, instructiondecodesimple_1_jxx, instructiondecodesimple_1_call);
  not not_1 (not_1_out, counter_1_q[0]);
  not not_2 (not_2_out, counter_1_q[1]);
  not not_3 (not_3_out, counter_1_q[2]);
  not not_4 (not_4_out, counter_1_q[3]);
  Comparator comparator_1 (.a(counter_1_q), .b(8'ha), .eq(resetEqual));  // open: gt, lt
  and and_1 (byte0, not_1_out, not_2_out, not_3_out, not_4_out);
  and and_2 (byte1, counter_1_q[0], not_2_out, not_3_out, not_4_out, byte1en_out);
  and and_3 (byte2, not_1_out, counter_1_q[1], not_3_out, not_4_out, bytevalC_out);
  and and_4 (byte3, counter_1_q[0], counter_1_q[1], not_3_out, not_4_out, bytevalC_out);
  and and_5 (byte4, not_1_out, not_2_out, counter_1_q[2], not_4_out, bytevalC_out);
  and and_6 (byte5, counter_1_q[0], not_2_out, counter_1_q[2], not_4_out, bytevalC_out);
  and and_7 (byte6, not_1_out, counter_1_q[1], counter_1_q[2], not_4_out, bytevalC_out);
  and and_8 (byte7, counter_1_q[0], counter_1_q[1], counter_1_q[2], not_4_out, bytevalC_out);
  and and_9 (byte8, not_1_out, not_2_out, not_3_out, counter_1_q[3], bytevalC_out);
  and and_10 (byte9, counter_1_q[0], not_2_out, not_3_out, counter_1_q[3], bytevalC_out);
  // AND_Gate byte10 has open pins: in0=not_1_out, in1=counter_1_q[1], in2=not_3_out, in3=counter_1_q[3], out=open
  // AND_Gate byte11 has open pins: in0=counter_1_q[0], in1=counter_1_q[1], in2=not_3_out, in3=counter_1_q[3], out=open

  // Notes on the sheet:
  //   equal?
  //   add clock as input so enable only works when clock is ticked.
  //   use input value from icode to determine if  registers 1 - 10 are enabled
endmodule

module fetchMain (
  input  [11:0] PC,
  input  clk,
  output [3:0] iCode,
  output haltstate,
  output [3:0] iFun,
  output [3:0] rA,
  output [3:0] rB,
  output [63:0] ValC,
  output [11:0] increment,
  output [11:0] valP
);

  wire and_1_out, comparator_1_eq, comparator_2_eq, comparator_3_eq, comparator_4_gt,
       controlled_buffer_1_out, fetchenable_1_byte0, fetchenable_1_byte1, fetchenable_1_byte2,
       fetchenable_1_byte3, fetchenable_1_byte4, fetchenable_1_byte5, fetchenable_1_byte6,
       fetchenable_1_byte7, fetchenable_1_byte8, fetchenable_1_byte9, not_1_out, not_2_out,
       oppositenull_1_byte1, oppositenull_1_byte2, oppositenull_1_byte3, oppositenull_1_byte4,
       oppositenull_1_byte5, oppositenull_1_byte6, oppositenull_1_byte7, oppositenull_1_byte8,
       oppositenull_1_byte9, or_1_out;
  wire [3:0] multiplexer_1_out, multiplexer_2_out;
  wire [7:0] multiplexer_3_out, multiplexer_4_out, multiplexer_5_out, multiplexer_6_out, multiplexer_7_out,
       multiplexer_8_out, multiplexer_9_out, multiplexer_10_out, register_6_q, register_7_q, register_8_q,
       register_9_q, register_10_q, register_11_q, register_12_q, register_13_q, rom_1_data;
  wire [11:0] adder_1_out, adder_2_out, counter_1_q, valpdecoder_1_p_inc;

  not not_1 (not_1_out, controlled_buffer_1_out);
  Comparator #(.width(12)) comparator_1 (
    .a(counter_1_q), .b(valpdecoder_1_p_inc), .eq(comparator_1_eq));  // open: gt, lt
  Counter #(.max('hfff), .width(12)) counter_1 (
    .clr(and_1_out), .clk(not_1_out), .Q(counter_1_q));  // open: load, up, count, D, carry
  Comparator #(.width(12)) comparator_2 (.a({12{1'b0}}), .b(adder_1_out), .eq(comparator_2_eq));  // open: gt, lt
  not not_2 (not_2_out, comparator_2_eq);
  assign controlled_buffer_1_out = or_1_out ? clk : 1'bz;  // Controlled_Buffer controlled_buffer_1
  and and_1 (and_1_out, comparator_1_eq, not_2_out);
  Adder #(.width(12)) adder_1 (.a(PC), .b(counter_1_q), .out(adder_1_out));  // open: cin, cout
  ROM #(.addrWidth(12)) rom_1 (.addr(adder_1_out), .data(rom_1_data));
  fetchEnable fetchenable_1 (
    .bytetrack({8{1'b0}}), .p_inc(8'ha), .clk(clk), .icode(iCode), .iFUN(iFun), .byte0(fetchenable_1_byte0),
    .byte1(fetchenable_1_byte1), .byte2(fetchenable_1_byte2), .byte3(fetchenable_1_byte3),
    .byte4(fetchenable_1_byte4), .byte5(fetchenable_1_byte5), .byte6(fetchenable_1_byte6),
    .byte7(fetchenable_1_byte7), .byte8(fetchenable_1_byte8), .byte9(fetchenable_1_byte9));  // open: resetEqual
  or or_1 (or_1_out, fetchenable_1_byte0, fetchenable_1_byte1, fetchenable_1_byte2, fetchenable_1_byte3, fetchenable_1_byte4, fetchenable_1_byte5, fetchenable_1_byte6, fetchenable_1_byte7, fetchenable_1_byte8, fetchenable_1_byte9);
  oppositeNULL oppositenull_1 (
    .clk(clk), .iFUN(iFun), .byte1(oppositenull_1_byte1), .byte2(oppositenull_1_byte2),
    .byte3(oppositenull_1_byte3), .byte4(oppositenull_1_byte4), .byte5(oppositenull_1_byte5),
    .byte6(oppositenull_1_byte6), .byte7(oppositenull_1_byte7), .byte8(oppositenull_1_byte8),
    .byte9(oppositenull_1_byte9));  // open: byte0, resetEqual
  ValPDecoder valpdecoder_1 (.icode(iCode), .P_inc(valpdecoder_1_p_inc));  // open: STOP
  Adder #(.width(12)) adder_2 (.a(valpdecoder_1_p_inc), .b(PC), .out(adder_2_out));  // open: cin, cout
  Multiplexer #(.width(4)) multiplexer_1 (
    .in0(4'b1111), .in1(rom_1_data[7:4]), .out(multiplexer_1_out), .sel(fetchenable_1_byte1));
  Multiplexer #(.width(4)) multiplexer_2 (
    .in0(4'b1111), .in1(rom_1_data[3:0]), .out(multiplexer_2_out), .sel(fetchenable_1_byte1));
  Multiplexer #(.width(8)) multiplexer_3 (
    .in0({8{1'b1}}), .in1(rom_1_data), .out(multiplexer_3_out), .sel(fetchenable_1_byte2));
  Multiplexer #(.width(8)) multiplexer_4 (
    .in0({8{1'b1}}), .in1(rom_1_data), .out(multiplexer_4_out), .sel(fetchenable_1_byte3));
  Multiplexer #(.width(8)) multiplexer_5 (
    .in0({8{1'b1}}), .in1(rom_1_data), .out(multiplexer_5_out), .sel(fetchenable_1_byte4));
  Multiplexer #(.width(8)) multiplexer_6 (
    .in0({8{1'b1}}), .in1(rom_1_data), .out(multiplexer_6_out), .sel(fetchenable_1_byte5));
  Multiplexer #(.width(8)) multiplexer_7 (
    .in0({8{1'b1}}), .in1(rom_1_data), .out(multiplexer_7_out), .sel(fetchenable_1_byte6));
  Multiplexer #(.width(8)) multiplexer_8 (
    .in0({8{1'b1}}), .in1(rom_1_data), .out(multiplexer_8_out), .sel(fetchenable_1_byte7));
  Multiplexer #(.width(8)) multiplexer_9 (
    .in0({8{1'b1}}), .in1(rom_1_data), .out(multiplexer_9_out), .sel(fetchenable_1_byte8));
  Multiplexer #(.width(8)) multiplexer_10 (
    .in0({8{1'b1}}), .in1(rom_1_data), .out(multiplexer_10_out), .sel(fetchenable_1_byte9));
  Register #(.width(12)) register_1 (.D(adder_1_out), .en(clk), .clk(clk), .Q(increment));  // open: clr
  Register #(.width(4)) register_2 (.D(rom_1_data[7:4]), .en(fetchenable_1_byte0), .clk(clk), .Q(iCode));  // open: clr
  Register #(.width(4)) register_3 (.D(rom_1_data[3:0]), .en(fetchenable_1_byte0), .clk(clk), .Q(iFun));  // open: clr
  Register #(.width(4)) register_4 (.D(multiplexer_1_out), .en(oppositenull_1_byte1), .clk(clk), .Q(rA));  // open: clr
  Register #(.width(4)) register_5 (.D(multiplexer_2_out), .en(oppositenull_1_byte1), .clk(clk), .Q(rB));  // open: clr
  Register register_6 (.D(multiplexer_3_out), .en(oppositenull_1_byte2), .clk(clk), .Q(register_6_q));  // open: clr
  Register register_7 (.D(multiplexer_4_out), .en(oppositenull_1_byte3), .clk(clk), .Q(register_7_q));  // open: clr
  Register register_8 (.D(multiplexer_5_out), .en(oppositenull_1_byte4), .clk(clk), .Q(register_8_q));  // open: clr
  Register register_9 (.D(multiplexer_6_out), .en(oppositenull_1_byte5), .clk(clk), .Q(register_9_q));  // open: clr
  Register register_10 (.D(multiplexer_7_out), .en(oppositenull_1_byte6), .clk(clk), .Q(register_10_q));  // open: clr
  Register register_11 (.D(multiplexer_8_out), .en(oppositenull_1_byte7), .clk(clk), .Q(register_11_q));  // open: clr
  Register register_12 (.D(multiplexer_9_out), .en(oppositenull_1_byte8), .clk(clk), .Q(register_12_q));  // open: clr
  Register register_13 (.D(multiplexer_10_out), .en(oppositenull_1_byte9), .clk(clk), .Q(register_13_q));  // open: clr
  Register #(.width(12)) register_14 (.D(adder_2_out), .en(clk), .clk(clk), .Q(valP));  // open: clr
  Comparator #(.width(4)) comparator_3 (.a(iCode), .b(4'b0000), .eq(comparator_3_eq));  // open: gt, lt
  Comparator #(.width(12)) comparator_4 (.a(PC), .b({12{1'b0}}), .gt(comparator_4_gt));  // open: eq, lt
  and and_2 (haltstate, comparator_3_eq, comparator_4_gt);
  Register #(.width(64)) register_15 (
    .D({register_13_q, register_12_q, register_11_q, register_10_q, register_9_q, register_8_q, register_7_q, register_6_q}),
    .clk(clk), .Q(ValC));  // open: en, clr

  // Notes on the sheet:
  //   counter ticks 10 times every time
  //   and we need to fix the fetch stop and delay problem
  //   add buffer to clock and keep incermenting when halt is not on
  //   contents of rom_1 (hex, n*v repeats v):
  //   50 f a 7*0 50 3f 14 7*0 80 26 7*0 70 29 7*0 60 30 90
  //   one byte output from rom
  //   we have a clock input that ticks adder and byte
  //   counter: tracking the byte were on: start at byte 0
  //   depending on instruction: we enable n times, reset byte to 0
  //   input into enable: when byte = p_inc we clear
  //   updating PC with val P location to ROM
  //   comparator of 2 memory addresses: then reset counter? for write enable registers.
endmodule

module MEDecoder (
  input  [3:0] Icode,
  output ME
);

  wire and_1_out, and_2_out, and_3_out, and_4_out, and_5_out, and_6_out, not_1_out, not_2_out, not_3_out,
       not_4_out;

  not not_1 (not_1_out, Icode[0]);
  not not_2 (not_2_out, Icode[2]);
  not not_3 (not_3_out, Icode[3]);
  not not_4 (not_4_out, Icode[1]);
  and and_1 (and_1_out, not_1_out, Icode[1], not_2_out, not_3_out);
  and and_2 (and_2_out, Icode[0], Icode[1], not_2_out, not_3_out);
  and and_3 (and_3_out, not_1_out, Icode[1], Icode[2], not_3_out);
  and and_4 (and_4_out, not_1_out, not_4_out, not_2_out, Icode[3]);
  and and_5 (and_5_out, Icode[0], not_4_out, not_2_out, Icode[3]);
  and and_6 (and_6_out, not_1_out, Icode[1], not_2_out, Icode[3]);
  or or_1 (ME, and_1_out, and_2_out, and_3_out, and_4_out, and_5_out, and_6_out);
endmodule

module RegisterFile (
  input  [3:0] icode,
  input  [3:0] srcA,
  input  [3:0] srcB,
  input  ME,
  input  [63:0] valM,
  input  [63:0] valE,
  input  [3:0] dstM,
  input  [3:0] dstE,
  input  Enable,
  input  clk,
  output [63:0] valA,
  output [63:0] valB,
  output [63:0] rax,
  output [63:0] rcx,
  output [63:0] rdx,
  output [63:0] rbx,
  output [63:0] rsp,
  output [63:0] rbp,
  output [63:0] rsi,
  output [63:0] rdi,
  output [63:0] r8,
  output [63:0] r9,
  output [63:0] r10,
  output [63:0] r11,
  output [63:0] r12,
  output [63:0] r13,
  output [63:0] r14
);

  wire decoder_1_out8, decoder_1_out9, decoder_1_out10, decoder_1_out11, demultiplexer_2_out0,
       demultiplexer_2_out1, demultiplexer_2_out2, demultiplexer_2_out3, demultiplexer_2_out4,
       demultiplexer_2_out5, demultiplexer_2_out6, demultiplexer_2_out7, demultiplexer_2_out8,
       demultiplexer_2_out9, demultiplexer_2_out10, demultiplexer_2_out11, demultiplexer_2_out12,
       demultiplexer_2_out13, demultiplexer_2_out14, demultiplexer_2_out15, or_1_out, or_2_out;
  wire [3:0] multiplexer_2_out;
  wire [63:0] demultiplexer_1_out0, demultiplexer_1_out1, demultiplexer_1_out2, demultiplexer_1_out3,
       demultiplexer_1_out4, demultiplexer_1_out5, demultiplexer_1_out6, demultiplexer_1_out7,
       demultiplexer_1_out8, demultiplexer_1_out9, demultiplexer_1_out10, demultiplexer_1_out11,
       demultiplexer_1_out12, demultiplexer_1_out13, demultiplexer_1_out14, multiplexer_1_out,
       multiplexer_3_out, multiplexer_4_out;

  Demultiplexer #(.select(4), .width(64)) demultiplexer_1 (
    .out0(demultiplexer_1_out0), .out1(demultiplexer_1_out1), .out2(demultiplexer_1_out2),
    .out3(demultiplexer_1_out3), .out4(demultiplexer_1_out4), .out5(demultiplexer_1_out5),
    .out6(demultiplexer_1_out6), .out7(demultiplexer_1_out7), .out8(demultiplexer_1_out8),
    .out9(demultiplexer_1_out9), .out10(demultiplexer_1_out10), .out11(demultiplexer_1_out11),
    .out12(demultiplexer_1_out12), .out13(demultiplexer_1_out13), .out14(demultiplexer_1_out14),
    .in(multiplexer_1_out), .sel(multiplexer_2_out));  // open: out15
  Multiplexer #(.width(64)) multiplexer_1 (.in0(valM), .in1(valE), .out(multiplexer_1_out), .sel(ME));
  Multiplexer #(.width(4)) multiplexer_2 (.in0(dstM), .in1(dstE), .out(multiplexer_2_out), .sel(ME));
  Demultiplexer #(.select(4)) demultiplexer_2 (
    .out0(demultiplexer_2_out0), .out1(demultiplexer_2_out1), .out2(demultiplexer_2_out2),
    .out3(demultiplexer_2_out3), .out4(demultiplexer_2_out4), .out5(demultiplexer_2_out5),
    .out6(demultiplexer_2_out6), .out7(demultiplexer_2_out7), .out8(demultiplexer_2_out8),
    .out9(demultiplexer_2_out9), .out10(demultiplexer_2_out10), .out11(demultiplexer_2_out11),
    .out12(demultiplexer_2_out12), .out13(demultiplexer_2_out13), .out14(demultiplexer_2_out14),
    .out15(demultiplexer_2_out15), .in(Enable), .sel(multiplexer_2_out));
  Register #(.width(64)) rax0 (.D(demultiplexer_1_out0), .en(demultiplexer_2_out0), .clk(clk), .Q(rax));  // open: clr
  Register #(.width(64)) rcx1 (.D(demultiplexer_1_out1), .en(demultiplexer_2_out1), .clk(clk), .Q(rcx));  // open: clr
  Register #(.width(64)) rdx2 (.D(demultiplexer_1_out2), .en(demultiplexer_2_out2), .clk(clk), .Q(rdx));  // open: clr
  Register #(.width(64)) rbx3 (.D(demultiplexer_1_out3), .en(demultiplexer_2_out3), .clk(clk), .Q(rbx));  // open: clr
  Register #(.width(64)) rsp4 (.D(demultiplexer_1_out4), .en(demultiplexer_2_out4), .clk(clk), .Q(rsp));  // open: clr
  Register #(.width(64)) rbp5 (.D(demultiplexer_1_out5), .en(demultiplexer_2_out5), .clk(clk), .Q(rbp));  // open: clr
  Register #(.width(64)) rsi6 (.D(demultiplexer_1_out6), .en(demultiplexer_2_out6), .clk(clk), .Q(rsi));  // open: clr
  Register #(.width(64)) rdi7 (.D(demultiplexer_1_out7), .en(demultiplexer_2_out7), .clk(clk), .Q(rdi));  // open: clr
  Register #(.width(64)) r88 (.D(demultiplexer_1_out8), .en(demultiplexer_2_out8), .clk(clk), .Q(r8));  // open: clr
  Register #(.width(64)) r99 (.D(demultiplexer_1_out9), .en(demultiplexer_2_out9), .clk(clk), .Q(r9));  // open: clr
  Register #(.width(64)) r10a (.D(demultiplexer_1_out10), .en(demultiplexer_2_out10), .clk(clk), .Q(r10));  // open: clr
  Register #(.width(64)) r11b (.D(demultiplexer_1_out11), .en(demultiplexer_2_out11), .clk(clk), .Q(r11));  // open: clr
  Register #(.width(64)) r12c (.D(demultiplexer_1_out12), .en(demultiplexer_2_out12), .clk(clk), .Q(r12));  // open: clr
  Register #(.width(64)) r13d (.D(demultiplexer_1_out13), .en(demultiplexer_2_out13), .clk(clk), .Q(r13));  // open: clr
  Register #(.width(64)) r14e (.en(demultiplexer_2_out14), .clk(clk), .Q(r14));  // open: D, clr
  Register #(.width(64)) r15f (.en(demultiplexer_2_out15), .clk(clk));  // open: D, Q, clr
  Multiplexer #(.select(4), .width(64)) multiplexer_3 (
    .in0(rax), .in1(rcx), .in2(rdx), .in3(rbx), .in4(rsp), .in5(rbp), .in6(rsi), .in7(rdi), .in8(r8),
    .in9(r9), .in10(r10), .in11(r11), .in12(r12), .in13(r13), .in14(r14), .out(multiplexer_3_out), .sel(srcA));  // open: in15
  Multiplexer #(.select(4), .width(64)) multiplexer_4 (
    .in0(rax), .in1(rcx), .in2(rdx), .in3(rbx), .in4(rsp), .in5(rbp), .in6(rsi), .in7(rdi), .in8(r8),
    .in9(r9), .in10(r10), .in11(r11), .in12(r12), .in13(r13), .in14(r14), .out(multiplexer_4_out), .sel(srcB));  // open: in15
  Multiplexer #(.width(64)) multiplexer_5 (.in0(multiplexer_3_out), .in1(rsp), .out(valA), .sel(or_2_out));
  Multiplexer #(.width(64)) multiplexer_6 (.in0(multiplexer_4_out), .in1(rsp), .out(valB), .sel(or_1_out));
  or or_1 (or_1_out, or_2_out, decoder_1_out10);
  Decoder #(.enable("false"), .select(4)) decoder_1 (
    .out8(decoder_1_out8), .out9(decoder_1_out9), .out10(decoder_1_out10), .out11(decoder_1_out11),
    .sel(icode));  // open: out0, out1, out2, out3, out4, out5, out6, out7, out12, out13, out14, out15
  or or_2 (or_2_out, decoder_1_out8, decoder_1_out9, decoder_1_out11);
endmodule

module Decode (
  input  [3:0] rA,
  input  [63:0] valM,
  input  [63:0] valE,
  input  [3:0] rB,
  input  [3:0] dstM,
  input  [3:0] dstE,
  input  [3:0] iCode,
  input  clk,
  output [63:0] valA,
  output [63:0] valB,
  output [63:0] rax,
  output [63:0] rcx,
  output [63:0] rdx,
  output [63:0] rbx,
  output [63:0] rsp,
  output [63:0] rbp,
  output [63:0] rsi,
  output [63:0] rdi,
  output [63:0] r8,
  output [63:0] r9,
  output [63:0] r10,
  output [63:0] r11,
  output [63:0] r12,
  output [63:0] r13,
  output [63:0] r14
);

  wire decoder_1_out2, decoder_1_out4, decoder_1_out5, decoder_1_out6, decoder_1_out10, decoder_2_out2,
       decoder_2_out3, decoder_2_out5, decoder_2_out6, decoder_2_out8, decoder_2_out9, decoder_2_out10,
       decoder_2_out11, medecoder_1_me, or_1_out, or_2_out, or_3_out;
  wire [3:0] multiplexer_1_out, multiplexer_2_out;

  Decoder #(.enable("false"), .select(4)) decoder_1 (
    .out2(decoder_1_out2), .out4(decoder_1_out4), .out5(decoder_1_out5), .out6(decoder_1_out6),
    .out10(decoder_1_out10), .sel(iCode));  // open: out0, out1, out3, out7, out8, out9, out11, out12, out13, out14, out15
  Decoder #(.enable("false"), .select(4)) decoder_2 (
    .out2(decoder_2_out2), .out3(decoder_2_out3), .out5(decoder_2_out5), .out6(decoder_2_out6),
    .out8(decoder_2_out8), .out9(decoder_2_out9), .out10(decoder_2_out10), .out11(decoder_2_out11),
    .sel(iCode));  // open: out0, out1, out4, out7, out12, out13, out14, out15
  Multiplexer #(.width(4)) multiplexer_1 (.in0(4'b1111), .in1(rA), .out(multiplexer_1_out), .sel(or_2_out));
  or or_1 (or_1_out, decoder_1_out4, decoder_1_out2, decoder_1_out5, decoder_1_out6);
  or or_2 (or_2_out, decoder_1_out2, decoder_1_out4, decoder_1_out6, decoder_1_out10);
  Multiplexer #(.width(4)) multiplexer_2 (.in0(4'b1111), .in1(rB), .out(multiplexer_2_out), .sel(or_1_out));
  MEDecoder medecoder_1 (.Icode(iCode), .ME(medecoder_1_me));
  or or_3 (or_3_out, decoder_2_out2, decoder_2_out3, decoder_2_out5, decoder_2_out6, decoder_2_out11, decoder_2_out8, decoder_2_out9, decoder_2_out10);
  RegisterFile registerfile_1 (
    .icode(iCode), .srcA(multiplexer_1_out), .srcB(multiplexer_2_out), .ME(medecoder_1_me), .valM(valM),
    .valE(valE), .dstM(dstM), .dstE(dstE), .Enable(or_3_out), .clk(clk), .valA(valA), .valB(valB), .rax(rax),
    .rcx(rcx), .rdx(rdx), .rbx(rbx), .rsp(rsp), .rbp(rbp), .rsi(rsi), .rdi(rdi), .r8(r8), .r9(r9), .r10(r10),
    .r11(r11), .r12(r12), .r13(r13), .r14(r14));
endmodule

module Execute (
  input  clk,
  input  [3:0] ifun,
  input  [3:0] icode,
  input  [63:0] valA,
  input  [63:0] valB,
  input  [63:0] valC,
  output [63:0] valE,
  output zero,
  output sign,
  output overflow,
  output conditional
);

  wire ctr_1_setcc, decoder_1_out0, decoder_1_out1, decoder_1_out7, nor_1_out;
  wire [2:0] cc_1_co;
  wire [63:0] alu_1_vale, ctr_1_a, ctr_1_b;

  Decoder #(.enable("false"), .select(4)) decoder_1 (
    .out0(decoder_1_out0), .out1(decoder_1_out1), .out7(decoder_1_out7), .sel(icode));  // open: out2, out3, out4, out5, out6, out8, out9, out10, out11, out12, out13, out14, out15
  ALU alu_1 (.A(ctr_1_a), .B(ctr_1_b), .iFun(ifun[1:0]), .icode(icode), .valE(alu_1_vale));
  CTR ctr_1 (.icode(icode), .valA(valA), .valB(valB), .valC(valC), .A(ctr_1_a), .B(ctr_1_b), .setCC(ctr_1_setcc));
  nor nor_1 (nor_1_out, decoder_1_out0, decoder_1_out1, decoder_1_out7);
  Register #(.width(64)) register_1 (.D(alu_1_vale), .en(nor_1_out), .clk(clk), .Q(valE));  // open: clr
  Flags flags_1 (
    .valE(alu_1_vale), .ifUn(ifun[1:0]), .A(ctr_1_a), .B(ctr_1_b), .zero(zero), .sign(sign),
    .overflow(overflow));
  CC cc_1 (.actuallCC({overflow, sign, zero}), .set(ctr_1_setcc), .clk(clk), .Co(cc_1_co));
  Cnd cnd_1 (.Co(cc_1_co), .ifun(ifun), .Cnd(conditional));
endmodule

module Cnd (
  input  [2:0] Co,
  input  [3:0] ifun,
  output Cnd
);

  wire decoder_1_out0, decoder_1_out1, decoder_1_out2, decoder_1_out3, decoder_1_out4, decoder_1_out5,
       decoder_1_out6, je_out, jg_out, jge_out, jl_out, jle_out, jne_out, not_1_out, not_2_out, not_3_out,
       not_4_out, or_1_out, xor_1_out;

  Decoder #(.enable("false"), .select(4)) decoder_1 (
    .out0(decoder_1_out0), .out1(decoder_1_out1), .out2(decoder_1_out2), .out3(decoder_1_out3),
    .out4(decoder_1_out4), .out5(decoder_1_out5), .out6(decoder_1_out6), .sel(ifun));  // open: out7, out8, out9, out10, out11, out12, out13, out14, out15
  xor xor_1 (xor_1_out, Co[1], Co[2]);
  or or_1 (or_1_out, xor_1_out, Co[0]);
  not not_1 (not_1_out, Co[0]);
  not not_2 (not_2_out, xor_1_out);
  not not_3 (not_3_out, xor_1_out);
  not not_4 (not_4_out, Co[0]);
  and jle (jle_out, or_1_out, decoder_1_out1);
  and jl (jl_out, xor_1_out, decoder_1_out2);
  and je (je_out, Co[0], decoder_1_out3);
  and jne (jne_out, not_1_out, decoder_1_out4);
  and jge (jge_out, not_2_out, decoder_1_out5);
  and jg (jg_out, not_3_out, decoder_1_out6, not_4_out);
  or or_2 (Cnd, decoder_1_out0, jle_out, jl_out, je_out, jne_out, jge_out, jg_out);

  // Notes on the sheet:
  //   0: zero 1:sign 2: overflow
endmodule

module ALUFun (
  input  [3:0] icode,
  output out_2
);

  wire not_1_out, not_2_out;

  not not_1 (not_1_out, icode[0]);
  and and_1 (out_2, not_1_out, icode[1], icode[2], not_2_out);
  not not_2 (not_2_out, icode[3]);
endmodule

module ALUA (
  input  [63:0] valA,
  input  [63:0] valC,
  input  [3:0] icode,
  output [63:0] A
);

  wire and_1_out, and_2_out, and_3_out, and_4_out, and_5_out, and_6_out, and_7_out, and_8_out, not_1_out,
       not_2_out, not_3_out, not_4_out;
  wire [3:0] C_out;

  not not_1 (not_1_out, icode[2]);
  not not_2 (not_2_out, icode[3]);
  not not_3 (not_3_out, icode[0]);
  not not_4 (not_4_out, icode[1]);
  Multiplexer #(.select(4), .width(64)) multiplexer_1 (
    .in0(valA), .in1(valC), .in2(64'h8), .in4(64'hfffffffffffffff8), .in8({64{1'b0}}), .out(A), .sel(C_out));  // open: in3, in5, in6, in7, in9, in10, in11, in12, in13, in14, in15
  and and_1 (and_1_out, icode[0], icode[1], not_1_out, not_2_out);
  and and_2 (and_2_out, not_3_out, not_4_out, icode[2], not_2_out);
  and and_3 (and_3_out, icode[0], not_4_out, icode[2], not_2_out);
  and and_4 (and_4_out, not_3_out, not_4_out, not_1_out, icode[3]);
  and and_5 (and_5_out, icode[0], not_4_out, not_1_out, icode[3]);
  and and_6 (and_6_out, not_3_out, icode[1], not_1_out, icode[3]);
  and and_7 (and_7_out, icode[0], icode[1], not_1_out, icode[3]);
  and and_8 (and_8_out, icode[0], icode[1], icode[2], not_2_out);
  or C (C_out[0], and_1_out, and_2_out, and_3_out);
  or eight (C_out[1], and_5_out, and_7_out);
  buf zero (C_out[3], and_8_out);  // OR_Gate
  or Neigth (C_out[2], and_4_out, and_6_out);
endmodule

module ALUB (
  input  [63:0] valB,
  input  [3:0] icode,
  output [63:0] B
);

  wire decoder_1_out2, decoder_1_out3, decoder_1_out7, or_1_out;

  Decoder #(.enable("false"), .select(4)) decoder_1 (
    .out2(decoder_1_out2), .out3(decoder_1_out3), .out7(decoder_1_out7), .sel(icode));  // open: out0, out1, out4, out5, out6, out8, out9, out10, out11, out12, out13, out14, out15
  Multiplexer #(.width(64)) multiplexer_1 (.in0(valB), .in1({64{1'b0}}), .out(B), .sel(or_1_out));
  or or_1 (or_1_out, decoder_1_out2, decoder_1_out3, decoder_1_out7);
endmodule

module CTR (
  input  [3:0] icode,
  input  [63:0] valA,
  input  [63:0] valB,
  input  [63:0] valC,
  output [63:0] A,
  output [63:0] B,
  output setCC
);

  wire not_1_out, not_2_out;

  not not_1 (not_1_out, icode[0]);
  not not_2 (not_2_out, icode[3]);
  ALUA alua_1 (.valA(valA), .valC(valC), .icode(icode), .A(A));
  ALUB alub_1 (.valB(valB), .icode(icode), .B(B));
  and and_1 (setCC, not_1_out, icode[1], icode[2], not_2_out);
endmodule

module Flags (
  input  [63:0] valE,
  input  [1:0] ifUn,
  input  [63:0] A,
  input  [63:0] B,
  output zero,
  output sign,
  output overflow
);

  wire and_1_out, and_2_out, comparator_1_lt, not_1_out, not_2_out, or_1_out;

  not not_1 (not_1_out, ifUn[1]);
  not not_2 (not_2_out, ifUn[0]);
  Comparator #(.width(64)) comparator_1 (.a(valE), .b({64{1'b0}}), .eq(zero), .lt(comparator_1_lt));  // open: gt
  and and_1 (and_1_out, ifUn[0], not_1_out);
  and and_2 (and_2_out, not_2_out, not_1_out);
  and and_3 (sign, comparator_1_lt, or_1_out);
  or or_1 (or_1_out, and_2_out, and_1_out);
  and and_4 (overflow, A[63], and_2_out, B[63]);
endmodule

module OPs (
  input  [63:0] A,
  input  [63:0] B,
  input  [1:0] ifun,
  output [63:0] valE
);

  wire [63:0] adder_1_out, and_1_out, subtractor_1_out, xor_1_out;

  Adder #(.width(64)) adder_1 (.a(A), .b(B), .out(adder_1_out));  // open: cin, cout
  Subtractor #(.width(64)) subtractor_1 (.a(B), .b(A), .out(subtractor_1_out));  // open: bin, bout
  assign and_1_out = A & B;  // AND_Gate and_1, 64 bits wide
  assign xor_1_out = A ^ B;  // XOR_Gate xor_1, 64 bits wide
  Multiplexer #(.select(2), .width(64)) multiplexer_1 (
    .in0(adder_1_out), .in1(subtractor_1_out), .in2(and_1_out), .in3(xor_1_out), .out(valE), .sel(ifun));
endmodule

module ALU (
  input  [63:0] A,
  input  [63:0] B,
  input  [1:0] iFun,
  input  [3:0] icode,
  output [63:0] valE
);

  wire alufun_1_out_2;
  wire [1:0] multiplexer_1_out;

  ALUFun alufun_1 (.icode(icode), .out_2(alufun_1_out_2));
  Multiplexer #(.width(2)) multiplexer_1 (.in0(2'b00), .in1(iFun), .out(multiplexer_1_out), .sel(alufun_1_out_2));
  OPs ops_1 (.A(A), .B(B), .ifun(multiplexer_1_out), .valE(valE));
endmodule

module CC (
  input  [2:0] actuallCC,
  input  set,
  input  clk,
  output [2:0] Co
);

  Register #(.width(3)) register_1 (.D(actuallCC), .en(set), .clk(clk), .Q(Co));  // open: clr
endmodule

module MemENABL (
  input  [3:0] in_1,
  output Address_enable,
  output write_enable,
  output writechoice,
  output read_enable,
  output readchoice
);

  wire call_out, mrmovq_out, not_1_out, not_2_out, not_3_out, not_4_out, or_3_out, pop_out, push_out,
       ret_out, rmmov_out;

  not not_1 (not_1_out, in_1[0]);
  not not_2 (not_2_out, in_1[1]);
  not not_3 (not_3_out, in_1[2]);
  not not_4 (not_4_out, in_1[3]);
  and rmmov (rmmov_out, not_1_out, not_2_out, in_1[2], not_4_out);
  and call (call_out, not_1_out, not_2_out, not_3_out, in_1[3]);
  and push (push_out, not_1_out, in_1[1], not_3_out, in_1[3]);
  and mrmovq (mrmovq_out, in_1[0], not_2_out, in_1[2], not_4_out);
  and ret (ret_out, in_1[0], not_2_out, not_3_out, in_1[3]);
  and pop (pop_out, in_1[0], in_1[1], not_3_out, in_1[3]);
  or or_1 (Address_enable, rmmov_out, mrmovq_out, call_out, push_out);
  or or_2 (write_enable, rmmov_out, call_out, push_out);
  or or_3 (or_3_out, ret_out, pop_out);
  or or_4 (read_enable, mrmovq_out, ret_out, pop_out);
  and and_1 (writechoice, call_out, write_enable);
  and and_2 (readchoice, read_enable, or_3_out);

  // Notes on the sheet:
  //   and gate makes sure read enable is on
  //   forgot what this does :/
  //   or gate  checks if it is ret or pop which uses valA, otherwise use val E
endmodule

module Memory (
  input  [3:0] icode,
  input  [63:0] valE,
  input  [63:0] valA,
  input  [11:0] valP,
  input  clk,
  output [63:0] valM
);

  wire comparator_1_eq, memenabl_1_read_enable, memenabl_1_readchoice, memenabl_1_write_enable,
       memenabl_1_writechoice, memory8bytecycle_1_byte1, memory8bytecycle_1_byte2, memory8bytecycle_1_byte3,
       memory8bytecycle_1_byte4, memory8bytecycle_1_byte5, memory8bytecycle_1_byte6,
       memory8bytecycle_1_byte7, memory8bytecycle_1_byte8, not_1_out, not_2_out;
  wire [1:0] counter_1_q_3;
  wire [2:0] counter_1_q, counter_1_q_2;
  wire [7:0] adder_1_out, multiplexer_1_out, multiplexer_2_out, multiplexer_3_out, multiplexer_4_out,
       ram_1_dout, register_1_q, register_2_q, register_3_q, register_4_q, register_5_q, register_6_q,
       register_7_q, register_8_q;

  Counter counter_1 (
    .clr(comparator_1_eq), .clk(not_1_out), .Q({counter_1_q_3, counter_1_q_2, counter_1_q}));  // open: load, up, count, D, carry
  not not_1 (not_1_out, clk);
  MemENABL memenabl_1 (
    .in_1(icode), .write_enable(memenabl_1_write_enable), .writechoice(memenabl_1_writechoice),
    .read_enable(memenabl_1_read_enable), .readchoice(memenabl_1_readchoice));  // open: Address_enable
  Multiplexer #(.select(3), .width(8)) multiplexer_1 (
    .in0(valA[7:0]), .in1(valA[15:8]), .in2(valA[23:16]), .in3(valA[31:24]), .in4(valA[39:32]),
    .in5(valA[47:40]), .in6(valA[55:48]), .in7(valA[63:56]), .out(multiplexer_1_out), .sel(counter_1_q));
  Multiplexer #(.select(3), .width(8)) multiplexer_2 (
    .in0(valP[7:0]), .in1({4'b0000, valP[11:8]}), .in2({8{1'b0}}), .in3({8{1'b0}}), .in4({8{1'b0}}),
    .in5({8{1'b0}}), .in6({8{1'b0}}), .in7({8{1'b0}}), .out(multiplexer_2_out), .sel(counter_1_q));
  Multiplexer #(.width(8)) multiplexer_3 (
    .in0(valE[7:0]), .in1(valA[7:0]), .out(multiplexer_3_out), .sel(memenabl_1_readchoice));
  Comparator comparator_1 (
    .a({counter_1_q_3, counter_1_q_2, counter_1_q}), .b(8'h8), .eq(comparator_1_eq));  // open: gt, lt
  Adder adder_1 (
    .a(multiplexer_3_out), .b({counter_1_q_3, counter_1_q_2, counter_1_q}), .out(adder_1_out));  // open: cin, cout
  Multiplexer #(.width(8)) multiplexer_4 (
    .in0(multiplexer_1_out), .in1(multiplexer_2_out), .out(multiplexer_4_out), .sel(memenabl_1_writechoice));
  memory8bytecycle memory8bytecycle_1 (
    .counter({counter_1_q_3, counter_1_q_2, counter_1_q}), .byte1(memory8bytecycle_1_byte1),
    .byte2(memory8bytecycle_1_byte2), .byte3(memory8bytecycle_1_byte3), .byte4(memory8bytecycle_1_byte4),
    .byte5(memory8bytecycle_1_byte5), .byte6(memory8bytecycle_1_byte6), .byte7(memory8bytecycle_1_byte7),
    .byte8(memory8bytecycle_1_byte8));
  RAM ram_1 (
    .addr(adder_1_out), .we(memenabl_1_write_enable), .clk(clk), .din(multiplexer_4_out), .dout(ram_1_dout));  // open: oe
  not not_2 (not_2_out, clk);
  Register register_1 (.D(ram_1_dout), .en(memory8bytecycle_1_byte1), .clk(not_2_out), .Q(register_1_q));  // open: clr
  Register register_2 (.D(ram_1_dout), .en(memory8bytecycle_1_byte2), .clk(not_2_out), .Q(register_2_q));  // open: clr
  Register register_3 (.D(ram_1_dout), .en(memory8bytecycle_1_byte3), .clk(not_2_out), .Q(register_3_q));  // open: clr
  Register register_4 (.D(ram_1_dout), .en(memory8bytecycle_1_byte4), .clk(not_2_out), .Q(register_4_q));  // open: clr
  Register register_5 (.D(ram_1_dout), .en(memory8bytecycle_1_byte5), .clk(not_2_out), .Q(register_5_q));  // open: clr
  Register register_6 (.D(ram_1_dout), .en(memory8bytecycle_1_byte6), .clk(not_2_out), .Q(register_6_q));  // open: clr
  Register register_7 (.D(ram_1_dout), .en(memory8bytecycle_1_byte7), .clk(not_2_out), .Q(register_7_q));  // open: clr
  Register register_8 (.D(ram_1_dout), .en(memory8bytecycle_1_byte8), .clk(not_2_out), .Q(register_8_q));  // open: clr
  assign valM = memenabl_1_read_enable ? {register_8_q, register_7_q, register_6_q, register_5_q, register_4_q, register_3_q, register_2_q, register_1_q} : 64'bz;  // Controlled_Buffer controlled_buffer_1

  // Notes on the sheet:
  //   read
  //   write
endmodule

module writeBack (
  input  [3:0] rA,
  input  [3:0] rB,
  input  [3:0] icode,
  input  clk,
  output [3:0] dstE,
  output [3:0] dstM
);

  wire comparator_1_eq, not_1_out;
  wire [3:0] controlled_buffer_1_out, multiplexer_1_out;

  Comparator #(.width(4)) comparator_1 (.a(icode), .b(4'b1011), .eq(comparator_1_eq));  // open: gt, lt
  Multiplexer #(.select(4), .width(4)) multiplexer_1 (
    .in2(rB), .in3(rB), .in5(rA), .in6(rB), .in8(4'b0100), .in9(4'b0100), .in10(4'b0100), .in11(rA),
    .out(multiplexer_1_out), .sel(icode));  // open: in0, in1, in4, in7, in12, in13, in14, in15
  assign controlled_buffer_1_out = comparator_1_eq ? 4'b0100 : 4'bz;  // Controlled_Buffer controlled_buffer_1
  not not_1 (not_1_out, comparator_1_eq);
  assign controlled_buffer_1_out = not_1_out ? multiplexer_1_out : 4'bz;  // Controlled_Buffer controlled_buffer_2
  Register #(.width(4)) register_1 (.D(controlled_buffer_1_out), .clk(clk), .Q(dstE));  // open: en, clr
  Register #(.width(4)) register_2 (.D(multiplexer_1_out), .clk(clk), .Q(dstM));  // open: en, clr

  // Notes on the sheet:
  //   add enable to decode
endmodule

module memory8bytecycle (
  input  [7:0] counter,
  output byte1,
  output byte2,
  output byte3,
  output byte4,
  output byte5,
  output byte6,
  output byte7,
  output byte8
);

  Comparator comparator_1 (.a(counter), .b({8{1'b0}}), .eq(byte1));  // open: gt, lt
  Comparator comparator_2 (.a(counter), .b(8'h1), .eq(byte2));  // open: gt, lt
  Comparator comparator_3 (.a(counter), .b(8'h2), .eq(byte3));  // open: gt, lt
  Comparator comparator_4 (.a(counter), .b(8'h3), .eq(byte4));  // open: gt, lt
  Comparator comparator_5 (.a(counter), .b(8'h4), .eq(byte5));  // open: gt, lt
  Comparator comparator_6 (.a(counter), .b(8'h5), .eq(byte6));  // open: gt, lt
  Comparator comparator_7 (.a(counter), .b(8'h6), .eq(byte7));  // open: gt, lt
  Comparator comparator_8 (.a(counter), .b(8'h7), .eq(byte8));  // open: gt, lt
endmodule

module PCupdate (
  input  [11:0] valP,
  input  [63:0] valC,
  input  cond,
  input  [3:0] icode,
  input  [63:0] valM,
  input  clk,
  output [11:0] newPC,
  output regupdate
);

  wire [7:0] multiplexer_1_out, multiplexer_2_out;

  Multiplexer #(.width(8)) multiplexer_1 (.in0(valP[7:0]), .in1(valC[7:0]), .out(multiplexer_1_out), .sel(cond));
  Multiplexer #(.select(4), .width(8)) multiplexer_2 (
    .in0({8{1'b0}}), .in1(valP[7:0]), .in2(valP[7:0]), .in3(valP[7:0]), .in4(valP[7:0]), .in5(valP[7:0]),
    .in6(valP[7:0]), .in7(multiplexer_1_out), .in8(valC[7:0]), .in9(valM[7:0]), .in10(valP[7:0]),
    .in11(valP[7:0]), .out(multiplexer_2_out), .sel(icode));  // open: in12, in13, in14, in15
  or or_1 (regupdate, clk, clk);
  Register #(.width(12)) register_1 (.D({4'b0000, multiplexer_2_out}), .clk(clk), .Q(newPC));  // open: en, clr
endmodule
